// Logisim project Aula01.circ as structural Verilog
module Novo (
  input  in_1,
  input  in_2,
  input  in_3,
  output out_4,
  output out_5,
  output out_6
);

  wire nand_1_out, or_1_out;

  and and_1 (out_4, in_1, in_2);
  nand nand_1 (nand_1_out, in_1, in_2);
  or or_1 (or_1_out, in_2, in_1);
  and and_2 (out_5, nand_1_out, or_1_out);

  // Other names for the same wires on the sheet: A = in_1; B = in_2; C = in_3; X = out_4; Y = out_5; Z = out_6
endmodule

module Desafio (
  input  in_1,
  input  in_2,
  input  in_3,
  output [1:0] out_4
);

  wire and_1_out, and_2_out, and_3_out, and_4_out, and_5_out, and_6_out, xor_1_out;

  and and_1 (and_1_out, in_1, in_2);
  and and_2 (and_2_out, in_1, in_3);
  and and_3 (and_3_out, in_2, in_3);
  and and_4 (and_4_out, and_1_out, ~in_3);  // AND_Gate
  and and_5 (and_5_out, ~in_1, and_3_out);  // AND_Gate
  or or_1 (out_4[1], and_4_out, and_2_out, and_5_out);
  ExactlyOne xor_1 (.out(xor_1_out), .in0(in_1), .in1(in_2), .in2(in_3));
  and and_6 (and_6_out, in_1, in_2, in_3);
  xor xor_2 (out_4[0], xor_1_out, and_6_out);

  // Other names for the same wires on the sheet: A = in_1; B = in_2; C = in_3; Y = out_4[0]; X = out_4[1]
endmodule
