// Logisim project Aula02.circ as structural Verilog
module \Aritmética  (
  input  [3:0] in_1,
  input  [3:0] in_2,
  input  [3:0] in_3,
  input  [3:0] in_4,
  input  [1:0] in_5,
  input  [1:0] in_6,
  input  [3:0] in_7,
  input  [7:0] in_8,
  input  [7:0] in_9,
  output [7:0] out_10
);

  wire [3:0] demultiplexer_1_out0, demultiplexer_1_out1, demultiplexer_1_out2, demultiplexer_1_out3,
       multiplexer_1_out;

  // Probe on multiplexer_1_out
  Multiplexer #(.select(2), .width(4)) multiplexer_1 (
    .in0(in_1), .in1(in_2), .in2(in_4), .in3(in_7), .out(multiplexer_1_out), .sel(in_5));  // open: en
  // Probe on out_10
  Adder adder_1 (.a(in_8), .b(in_9), .out(out_10));  // open: cin, cout
  Demultiplexer #(.select(2), .width(4)) demultiplexer_1 (
    .out0(demultiplexer_1_out0), .out1(demultiplexer_1_out1), .out2(demultiplexer_1_out2),
    .out3(demultiplexer_1_out3), .in(in_3), .sel(in_6));  // open: en
  // Probe on demultiplexer_1_out0
  // Probe on demultiplexer_1_out3
  // Probe on demultiplexer_1_out1
  // Probe on demultiplexer_1_out2
endmodule

module Calculadora (
  input  [7:0] in_1,
  input  [1:0] in_2,
  input  [7:0] in_3
);

  wire [7:0] adder_1_out, D1, D2, divider_1_out, M1, M2, multiplier_1_out, Res, S1, S2, Sub1, Sub2,
       subtractor_1_out;

  // Probe on Res
  // Probe on in_1
  // Probe on in_2
  // Probe on in_3
  Adder adder_1 (.a(S1), .b(S2), .out(adder_1_out));  // open: cin, cout
  Subtractor subtractor_1 (.a(Sub1), .b(Sub2), .out(subtractor_1_out));  // open: bin, bout
  Multiplier multiplier_1 (.a(M2), .b(M1), .out(multiplier_1_out));  // open: cin, cout
  Divider divider_1 (.a(D2), .b(D1), .out(divider_1_out));  // open: upper, rem
  Demultiplexer #(.select(2), .width(8)) demultiplexer_1 (
    .out0(S1), .out1(Sub1), .out2(M1), .out3(D1), .in(in_1), .sel(in_2));  // open: en
  Demultiplexer #(.select(2), .width(8)) demultiplexer_2 (
    .out0(S2), .out1(Sub2), .out2(M2), .out3(D2), .in(in_3), .sel(in_2));  // open: en
  Multiplexer #(.select(2), .width(8), .disabled(0), .enable("false")) multiplexer_1 (
    .in0(adder_1_out), .in1(subtractor_1_out), .in2(multiplier_1_out), .in3(divider_1_out), .out(Res),
    .sel(in_2));
  ULA ula_1 ();  // open: in_1, in_2, in_3, A_B_3, A_B_2, A_B, out_4
  RAM ram_1 ();  // open: addr, data, sel, clk, ld, clr

  // Other names for the same wires on the sheet: N1[7:0] = in_1; N2[7:0] = in_3; Op[1:0] = in_2
endmodule

module ULA (
  input  [15:0] in_1,
  input  [15:0] in_2,
  input  [3:0] in_3,
  output [15:0] out_4,
  output A_B,
  output A_B_2,
  output A_B_3
);

  wire [15:0] AND, ANegatorOut, Decrement, Div, Increment, LeftShiftOut, Mult, NotA, OR, RightShiftOut, Sub,
       Sum, undriven, undriven_2, undriven_3, XOR;

  Adder #(.width(16)) adder_1 (.a(in_1), .b(in_2), .out(Sum));  // open: cin, cout
  Adder #(.width(16)) adder_2 (.a(in_1), .b(in_2), .out(Sub));  // open: cin, cout
  Adder #(.width(16)) adder_3 (.a(in_1), .b(in_2), .out(Mult));  // open: cin, cout
  Adder #(.width(16)) adder_4 (.a(in_1), .b(in_2), .out(Div));  // open: cin, cout
  Adder #(.width(16)) adder_5 (.a(in_1), .b(16'h1), .out(Increment));  // open: cin, cout
  Adder #(.width(16)) adder_6 (.a(in_1), .b(16'h1), .out(Decrement));  // open: cin, cout
  assign NotA = ~in_1;  // NOT_Gate not_1, 16 bits wide
  assign AND = in_1 & in_2;  // AND_Gate and_1, 16 bits wide
  assign OR = in_1 | in_2;  // OR_Gate or_1, 16 bits wide
  assign XOR = in_1 ^ in_2;  // XOR_Gate xor_1, 16 bits wide
  Shifter #(.width(16), .shift("lr")) shifter_1 (.in(in_1), .\dist (in_2[3:0]), .out(RightShiftOut));
  Shifter #(.width(16)) shifter_2 (.in(in_1), .\dist (in_2[3:0]), .out(LeftShiftOut));
  Negator #(.width(16)) negator_1 (.in(in_1), .out(ANegatorOut));
  Comparator #(.width(16)) comparator_1 (.a(in_1), .b(in_2), .gt(A_B), .eq(A_B_2), .lt(A_B_3));
  Multiplexer #(.select(4), .width(16)) multiplexer_1 (
    .in0(Sum), .in1(Sub), .in2(Mult), .in3(Div), .in4(Increment), .in5(Decrement), .in6(NotA), .in7(AND),
    .in8(OR), .in9(XOR), .in10(RightShiftOut), .in11(LeftShiftOut), .in12(ANegatorOut), .in13(undriven),
    .in14(undriven_2), .in15(undriven_3), .out(out_4), .sel(in_3));  // open: en

  // Other names for the same wires on the sheet: Control[3:0] = in_3; IA[15:0] = in_1; IB[15:0] = in_2
endmodule
