// Logisim project Aula03.circ as structural Verilog
module Latch_RS (
  input  Set,
  input  Reset,
  output out_3
);

  wire and_1_out, and_2_out, not_2_out;

  not not_1 (out_3, and_1_out);
  and and_1 (and_1_out, Set, not_2_out);
  not not_2 (not_2_out, and_2_out);
  and and_2 (and_2_out, out_3, Reset);
endmodule

module Latch_D (
  input  in_1,
  input  in_2,
  output out_3
);

  wire and_1_out, and_2_out, not_1_out, not_2_out, not_3_out;

  not not_1 (not_1_out, in_1);
  not not_2 (not_2_out, and_1_out);
  and and_1 (and_1_out, in_1, in_2);
  not not_3 (not_3_out, and_2_out);
  and and_2 (and_2_out, in_2, not_1_out);
  Latch_RS latch_rs_1 (.Set(not_2_out), .Reset(not_3_out), .out_3(out_3));
endmodule

module Flip_Flop_D (
  input  Data,
  input  Enable,
  input  Clock,
  output out_4
);

  wire and_1_out, latch_d_1_out_3, not_1_out;

  and and_1 (and_1_out, Enable, Clock);
  Latch_D latch_d_1 (.in_1(Data), .in_2(and_1_out), .out_3(latch_d_1_out_3));
  not not_1 (not_1_out, Clock);
  Latch_D latch_d_2 (.in_1(latch_d_1_out_3), .in_2(not_1_out), .out_3(out_4));
endmodule

module Gerador_de_Clock (
  input  in_1,
  output out_2
);

  wire and_1_out, clock_1_out, flip_flop_d_1_out_4, not_1_out;

  Clock clock_1 (.out(clock_1_out));
  not not_1 (not_1_out, flip_flop_d_1_out_4);
  Flip_Flop_D flip_flop_d_1 (.Data(in_1), .Enable(1'b1), .Clock(clock_1_out), .out_4(flip_flop_d_1_out_4));
  and and_1 (and_1_out, in_1, not_1_out);
  Flip_Flop_D flip_flop_d_2 (.Data(and_1_out), .Enable(1'b1), .Clock(clock_1_out), .out_4(out_2));
endmodule

module Registradores (
  input  [1:0] in_1,
  input  [1:0] in_2,
  input  in_3,
  input  in_4,
  input  [3:0] in_5,
  input  [1:0] in_6,
  input  in_7,
  output [3:0] out_8,
  output [3:0] out_9
);

  wire E1, E2, E3, R1, R2, R3;
  wire [3:0] DataR1, DataR2, DataR3, RAO, RBO, RCO;

  Register #(.width(4)) register_1 (.D(DataR1), .en(E1), .Q(RAO), .clk(in_4), .clr(R1));
  Demultiplexer #(.select(2), .width(4)) demultiplexer_1 (
    .out0(DataR1), .out1(DataR2), .out2(DataR3), .in(in_5), .sel(in_1));  // open: out3, en
  Demultiplexer #(.select(2)) demultiplexer_2 (
    .out0(E1), .out1(E2), .out2(E3), .in(in_3), .sel(in_1));  // open: out3, en
  Demultiplexer #(.select(2)) demultiplexer_3 (
    .out0(R1), .out1(R2), .out2(R3), .in(1'b1), .sel(in_6), .en(in_7));  // open: out3
  Register #(.width(4)) register_2 (.D(DataR2), .en(E2), .Q(RBO), .clk(in_4), .clr(R2));
  Multiplexer #(.select(2), .width(4)) multiplexer_1 (
    .in0(RAO), .in1(RBO), .in2(RCO), .out(out_9), .sel(in_1));  // open: in3, en
  Multiplexer #(.select(2), .width(4)) multiplexer_2 (
    .in0(RAO), .in1(RBO), .in2(RCO), .out(out_8), .sel(in_2));  // open: in3, en
  Register #(.width(4)) register_3 (.D(DataR3), .en(E3), .Q(RCO), .clk(in_4), .clr(R3));

  // Other names for the same wires on the sheet: C = in_4; Data[3:0] = in_5; E = in_3; EA[1:0] = in_1; EB[1:0] = in_2;
  //   ER[1:0] = in_6; R = in_7

  // Notes on the sheet:
  //   Reg 1
  //   Define Registrador
  //   Liga o enable
  //   Reseta o Registrador
  //   Reg 2
  //   Pega o valor do Registrador EA
  //   Reg 3
  //   Pega valor do Registrador EB
endmodule

module Teste (
  input  [3:0] in_1,
  input  [1:0] in_2,
  input  [1:0] in_3,
  input  [1:0] in_4,
  input  in_5,
  input  in_6,
  input  in_7,
  input  [31:0] in_8,
  input  [31:0] in_9,
  input  [31:0] in_10,
  input  [31:0] in_11,
  input  [31:0] in_12,
  input  [31:0] in_13,
  input  [31:0] in_14,
  input  [31:0] in_15,
  input  [31:0] in_16,
  input  [31:0] in_17,
  input  [31:0] in_18,
  input  [31:0] in_19,
  input  [31:0] in_20,
  input  [31:0] in_21,
  input  [31:0] in_22,
  input  [31:0] in_23,
  input  [31:0] in_24,
  input  [31:0] in_25,
  input  [31:0] in_26,
  input  [31:0] in_27,
  input  [31:0] in_28,
  input  [31:0] in_29,
  input  [31:0] in_30,
  input  [31:0] in_31,
  input  [31:0] in_32,
  input  [31:0] in_33,
  input  [31:0] in_34,
  input  [31:0] in_35,
  input  [31:0] in_36,
  input  [31:0] in_37,
  input  [31:0] in_38,
  input  [31:0] in_39,
  output [3:0] out_40,
  output [3:0] out_41
);

  wire clock_1_out;

  Hex_Digit_Display hex_digit_display_1 ();  // open: value, dp
  Keyboard keyboard_1 (.clr(in_7));  // open: clk, re, avail, data
  _7_Segment_Display u_7_segment_display_1 ();  // open: g, f, a, b, e, d, c, dp
  // Probe on in_1
  Registradores registradores_1 (
    .in_1(in_2), .in_2(in_4), .in_3(in_6), .in_5(in_1), .in_6(in_3), .in_7(in_5), .in_4(clock_1_out),
    .out_8(out_40), .out_9(out_41));
  Clock clock_1 (.out(clock_1_out));
  // Probe on out_41
  // Probe on out_40
  DotMatrix #(.matrixcols(32), .matrixrows(32)) dotmatrix_1 (
    .col0(in_8), .col1(in_10), .col2(in_12), .col3(in_14), .col4(in_16), .col5(in_18), .col6(in_20),
    .col7(in_22), .col8(in_24), .col9(in_26), .col10(in_28), .col11(in_30), .col12(in_32), .col13(in_34),
    .col14(in_36), .col15(in_38), .col16(in_39), .col17(in_35), .col18(in_35), .col19(in_33), .col20(in_31),
    .col21(in_29), .col22(in_27), .col23(in_25), .col24(in_23), .col25(in_21), .col26(in_19), .col27(in_17),
    .col28(in_15), .col29(in_13), .col30(in_11), .col31(in_9));

  assign in_37 = in_35;
endmodule
